// Logisim project adders.circ as structural Verilog: 3 circuits, main circuit main
module main (
  input  x1,
  input  y1,
  input  x2,
  input  y2,
  input  x3,
  input  y3,
  input  x3_2,
  input  y3_2,
  input  c,
  output a5,
  output a4,
  output a1,
  output a2,
  output a3
);

  wire adder_1_cout, adder_2_cout, adder_3_cout;

  adder adder_1 (.x(x1), .y(y1), .Cin(c), .cout(adder_1_cout), .Sum(a1));
  adder adder_2 (.x(adder_1_cout), .y(y2), .Cin(x2), .cout(adder_2_cout), .Sum(a2));
  adder adder_3 (.x(adder_2_cout), .y(x3), .Cin(y3), .cout(adder_3_cout), .Sum(a3));
  adder adder_4 (.x(adder_3_cout), .y(x3_2), .Cin(y3_2), .cout(a5), .Sum(a4));
endmodule

module adder (
  input  x,
  input  y,
  input  Cin,
  output cout,
  output Sum
);

  wire and_1_out, and_2_out, and_3_out, and_4_out, and_5_out, and_6_out, and_7_out, and_8_out, and_9_out,
       and_10_out, and_11_out, not_1_out, not_2_out, not_3_out, not_4_out, not_5_out, not_6_out, or_1_out,
       or_3_out, or_4_out;

  and and_1 (and_1_out, y, Cin);
  and and_2 (and_2_out, x, Cin);
  not not_1 (not_1_out, x);
  not not_2 (not_2_out, y);
  not not_3 (not_3_out, y);
  not not_4 (not_4_out, x);
  or or_1 (or_1_out, and_1_out, and_2_out);
  and and_3 (and_3_out, x, y);
  and and_4 (and_4_out, not_1_out, not_2_out);
  and and_5 (and_5_out, x, not_3_out);
  not not_5 (not_5_out, Cin);
  and and_6 (and_6_out, y, not_4_out);
  not not_6 (not_6_out, Cin);
  and and_7 (and_7_out, x, y);
  or or_2 (cout, or_1_out, and_3_out);
  and and_8 (and_8_out, and_4_out, Cin);
  and and_9 (and_9_out, and_5_out, not_5_out);
  and and_10 (and_10_out, and_6_out, not_6_out);
  and and_11 (and_11_out, and_7_out, Cin);
  or or_3 (or_3_out, and_8_out, and_9_out);
  or or_4 (or_4_out, and_10_out, and_11_out);
  or or_5 (Sum, or_3_out, or_4_out);
endmodule

module half_adder (
  input  a,
  input  b,
  output x,
  output y
);

  xor xor_1 (x, a, b);
  and and_1 (y, b, a);
endmodule
